# Fritzing sketch seması (saved by Fritzing 0.9.10b)

parts:
  M1 = STM32F103C8T6 blue mini board
  Parça2 = NRF24L01
  R1 = Resistor [tolerance=±5% resistance=220 package="0603 [SMD]"]
  S5 = Round Pushbutton
  Parça3 = NRF24L01
  Mod1 = Amica NodeMCU DEVKIT 1.0
  R2 = Resistor [tolerance=±5% resistance=220 package="0603 [SMD]"]
  LED1 = smd LED [color="Red (633nm)" package="0805 [SMD]"]

nets:
  N1: M1.B4, Parça2.CE
  N2: M1.B5, Parça2.CSN
  N3: M1.A0, R1.Pin_1, S5.leg0
  N4: M1.A5, Parça2.SCK
  N5: M1.A6, Parça2.MISO
  N6: M1.A7, Parça2.MOSI
  3.3V: M1.3.3V, M1.3.3, Parça2.VCC, S5.leg1
  GND: M1.G, M1.GND, Parça2.GND, R1.Pin_0
  N7: Parça3.MOSI, Mod1.pin6
  N8: Parça3.CSN, Mod1.pin_13
  N9: Parça3.VCC, Mod1.pin_26
  N10: Parça3.MISO, Mod1.pin7
  N11: Parça3.SCK, Mod1.pin8
  N12: Parça3.CE, Mod1.pin_11
  N13: Parça3.GND, Mod1.pin_25, Mod1.pin_29, LED1.cathode
  N14: Mod1.pin_15, R2.Pin_1
  N15: R2.Pin_0, LED1.anode
